# Fritzing sketch scheme (saved by Fritzing 1.0.6)

parts:
  J1 = female pin header, 5 pins [form="♀ (female)"]
  RP_Pico = Raspberry Pi Pico
  LLC1 = Logic Level Converter [package="Breakout board"]
  Reset = Momentary Switch [package=ksa_sealed_tac_switch]

nets:
  N1: J1.pin1, LLC1.H-GND
  N2: J1.pin2, LLC1.HV3
  N3: J1.pin3, LLC1.HV2
  N4: J1.pin4, LLC1.HV1
  N5: J1.pin5, RP_Pico.pin_39, LLC1.HV
  N6: RP_Pico.pin_3, RP_Pico.pin_28, LLC1.L-GND, Reset.2
  N7: RP_Pico.pin_4, LLC1.LV3
  N8: RP_Pico.pin_5, LLC1.LV2
  N9: RP_Pico.pin_6, LLC1.LV1
  N10: RP_Pico.pin_30, Reset.4
  N11: RP_Pico.pin_36, LLC1.LV

notes:
  VBUS - VCC
  GP4 - CLK
  GP3 - DATA
  GP2 - SEL
  GND - GND
  Reset

custom parts:
  Raspberry Pi Pico: Raspberry Pi Pico. Based around the RP2040 microcontroller the Pico is a low cost microcontroller device bringing Raspberry Pi quality, cost, and easy of use to the microcontroller space. Jan 2021, Split part in to two versions: tht (this one) and SMD. This one will drill holes for a .1 in header in pcb to allow plugging in the module as well as providing pads to solder the module to the top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
  Logic Level Converter: 5V to/from 3.3V logic level converter
